# Fritzing sketch raspi1 (saved by Fritzing 0.9.4)
breadboards: 1

parts:
  Raspberry_Pi_1 = Raspberry Pi 4 [part_number=RPI-4-b]
  OLED_I2C1 = OLED 128x64 I2C Monochrome Display
  DHT1 = DHT11 Humitidy and Temperature Sensor

nets:
  N1: Raspberry_Pi_1.GPIO2, OLED_I2C1.SDA
  N2: Raspberry_Pi_1.GPIO3, OLED_I2C1.SCK
  GND: Raspberry_Pi_1.GND, OLED_I2C1.GND, DHT1.NULL
  3V3: Raspberry_Pi_1.3V3, DHT1.VDD
  N3: Raspberry_Pi_1.GPIO14, DHT1.DATA
  5V: Raspberry_Pi_1.5V, OLED_I2C1.VDD

custom parts:
  Raspberry Pi 4: The RPi4, a faster version of the awesome Raspberry Pi 2 B ARM Board with 40 pin gpio. Ready for special Raspberry Pi B+ and RPi2 Hat (Hardware attached (on) top)
  DHT11 Humitidy and Temperature Sensor: DHT11 Humidity and Temperature Sensor
